// Logisim project CPU.circ as structural Verilog: 6 circuits, main circuit 1b ALU
module _1b_ALU (
  input  Cin,
  input  sub,
  input  A,
  input  B,
  input  [2:0] in_5,
  input  Neighbor_Right,
  input  Neighbor_Left,
  output out_8,
  output out_9
);

  wire adder_1_out, and_1_out, nand_1_out, not_1_out, or_1_out, xor_1_out, xor_2_out;

  xor xor_1 (xor_1_out, sub, A);
  Adder #(.width(1)) adder_1 (.a(xor_1_out), .b(B), .out(adder_1_out), .cin(Cin), .cout(out_8));
  not not_1 (not_1_out, B);
  nand nand_1 (nand_1_out, A, B);
  and and_1 (and_1_out, A, B);
  or or_1 (or_1_out, A, B);
  xor xor_2 (xor_2_out, A, B);
  Multiplexer #(.select(3), .enable("false")) multiplexer_1 (
    .in0(adder_1_out), .in1(nand_1_out), .in2(and_1_out), .in3(or_1_out), .in4(xor_2_out),
    .in5(Neighbor_Right), .in6(Neighbor_Left), .in7(not_1_out), .out(out_9), .sel(in_5));
endmodule

module ALU (
  input  [7:0] A,
  input  in_2,
  input  [2:0] in_3,
  input  [7:0] B,
  input  in_5,
  output [7:0] C,
  output out_7
);

  wire and_1_out, n1b_alu_1_out_8, n1b_alu_2_out_8, n1b_alu_3_out_8, n1b_alu_4_out_8, n1b_alu_5_out_8,
       n1b_alu_6_out_8, n1b_alu_7_out_8;

  and and_1 (and_1_out, B[7], in_5);
  _1b_ALU u_1b_alu_1 (
    .A(A[0]), .B(B[0]), .out_9(C[0]), .Cin(in_2), .in_5(in_3), .out_8(n1b_alu_1_out_8),
    .Neighbor_Right(1'b0), .Neighbor_Left(B[1]), .sub(in_2));
  _1b_ALU u_1b_alu_2 (
    .A(A[1]), .B(B[1]), .out_9(C[1]), .Cin(n1b_alu_1_out_8), .in_5(in_3), .out_8(n1b_alu_2_out_8),
    .Neighbor_Right(B[0]), .Neighbor_Left(B[2]), .sub(in_2));
  _1b_ALU u_1b_alu_3 (
    .A(A[2]), .B(B[2]), .out_9(C[2]), .Cin(n1b_alu_2_out_8), .in_5(in_3), .out_8(n1b_alu_3_out_8),
    .Neighbor_Right(B[1]), .Neighbor_Left(B[3]), .sub(in_2));
  _1b_ALU u_1b_alu_4 (
    .A(A[3]), .B(B[3]), .out_9(C[3]), .Cin(n1b_alu_3_out_8), .in_5(in_3), .out_8(n1b_alu_4_out_8),
    .Neighbor_Right(B[2]), .Neighbor_Left(B[4]), .sub(in_2));
  _1b_ALU u_1b_alu_5 (
    .A(A[4]), .B(B[4]), .out_9(C[4]), .Cin(n1b_alu_4_out_8), .in_5(in_3), .out_8(n1b_alu_5_out_8),
    .Neighbor_Right(B[3]), .Neighbor_Left(B[5]), .sub(in_2));
  _1b_ALU u_1b_alu_6 (
    .A(A[5]), .B(B[5]), .out_9(C[5]), .Cin(n1b_alu_5_out_8), .in_5(in_3), .out_8(n1b_alu_6_out_8),
    .Neighbor_Right(B[4]), .Neighbor_Left(B[6]), .sub(in_2));
  _1b_ALU u_1b_alu_7 (
    .A(A[6]), .B(B[6]), .out_9(C[6]), .Cin(n1b_alu_6_out_8), .in_5(in_3), .out_8(n1b_alu_7_out_8),
    .Neighbor_Right(B[5]), .Neighbor_Left(B[7]), .sub(in_2));
  _1b_ALU u_1b_alu_8 (
    .A(A[7]), .B(B[7]), .out_9(C[7]), .Cin(n1b_alu_7_out_8), .in_5(in_3), .out_8(out_7),
    .Neighbor_Right(B[6]), .Neighbor_Left(and_1_out), .sub(in_2));
endmodule

module Datapath (
  input  in_1
);

  wire CLK, clock_1_out, control_unit_1_accin, control_unit_1_accout, control_unit_1_aluout,
       control_unit_1_ash, control_unit_1_flagin, control_unit_1_hlt, control_unit_1_irin,
       control_unit_1_jeq, control_unit_1_jgt, control_unit_1_jlt, control_unit_1_jmp, control_unit_1_jne,
       control_unit_1_marin, control_unit_1_mdrin, control_unit_1_mdrin_ib_eb, control_unit_1_mdrout_ib_eb,
       control_unit_1_memread, control_unit_1_outin, control_unit_1_pcin, control_unit_1_pcout,
       control_unit_1_sub, JEQ_out, JGT_out, JLT_out, jmp_active, JNE_out, nand_1_out, Negative_Flag_q,
       Negative_Flag_qn, nor_1_out, nor_2_out, not_1_out, not_2_out, zero_flag_q, zero_flag_qn;
  wire [2:0] control_unit_1_aluop;
  wire [3:0] OUT_q, OUT_q_2;
  wire [7:0] ACC_q, adder_1_out, alu_1_p6, controlled_buffer_1_out, controlled_buffer_3_out, IR_q, MAR_q,
       MDR_q, multiplexer_1_out, multiplexer_2_out, multiplexer_3_out, PC_q, ram_1_data;

  Clock clock_1 (.out(clock_1_out));
  not not_1 (not_1_out, control_unit_1_hlt);
  and and_1 (CLK, clock_1_out, not_1_out);
  RAM ram_1 (.addr(MAR_q), .data(ram_1_data), .clk(CLK), .ld(not_2_out), .clr(in_1));  // open: sel
  not not_2 (not_2_out, control_unit_1_memread);
  Register MAR (.D(controlled_buffer_3_out), .en(control_unit_1_marin), .Q(MAR_q), .clk(CLK));  // open: clr
  nand nand_1 (nand_1_out, jmp_active, nor_1_out);
  assign controlled_buffer_1_out = nand_1_out ? multiplexer_2_out : 8'bz;  // Controlled_Buffer controlled_buffer_1
  assign ram_1_data = control_unit_1_memread ? MDR_q : 8'bz;  // Controlled_Buffer controlled_buffer_2
  Multiplexer #(.width(8), .enable("false")) multiplexer_1 (
    .in0(ram_1_data), .in1(controlled_buffer_3_out), .out(multiplexer_1_out), .sel(control_unit_1_mdrin_ib_eb));
  Register IR (.D(controlled_buffer_3_out), .en(control_unit_1_irin), .Q(IR_q), .clk(CLK));  // open: clr
  Control_Unit control_unit_1 (
    .IRin(control_unit_1_irin), .MARin(control_unit_1_marin), .MDRout_IB_EB(control_unit_1_mdrout_ib_eb),
    .PCin(control_unit_1_pcin), .MemRead(control_unit_1_memread), .sub(control_unit_1_sub), .IR(IR_q),
    .in_2(CLK), .MDRin(control_unit_1_mdrin), .ACCin(control_unit_1_accin), .ACCout(control_unit_1_accout),
    .PCout(control_unit_1_pcout), .ALUop(control_unit_1_aluop), .HLT(control_unit_1_hlt),
    .OUTin(control_unit_1_outin), .ash(control_unit_1_ash), .ALUout(control_unit_1_aluout),
    .JMP(control_unit_1_jmp), .JEQ(control_unit_1_jeq), .JNE(control_unit_1_jne), .JGT(control_unit_1_jgt),
    .JLT(control_unit_1_jlt), .Flagin(control_unit_1_flagin), .MDRin_IB_EB(control_unit_1_mdrin_ib_eb));
  Multiplexer #(.width(8), .enable("false")) multiplexer_2 (
    .in0(controlled_buffer_3_out), .in1(adder_1_out), .out(multiplexer_2_out), .sel(nor_1_out));
  Register PC (.D(controlled_buffer_1_out), .en(control_unit_1_pcin), .Q(PC_q), .clk(CLK));  // open: clr
  Adder adder_1 (.a(8'h1), .b(PC_q), .out(adder_1_out));  // open: cin, cout
  assign controlled_buffer_3_out = control_unit_1_pcout ? PC_q : 8'bz;  // Controlled_Buffer controlled_buffer_3
  Register MDR (.D(multiplexer_1_out), .en(control_unit_1_mdrin), .Q(MDR_q), .clk(CLK));  // open: clr
  or or_1 (jmp_active, control_unit_1_jlt, control_unit_1_jgt, control_unit_1_jeq, control_unit_1_jmp, control_unit_1_jne);
  nor nor_1 (nor_1_out, JNE_out, control_unit_1_jmp, JEQ_out, JGT_out, JLT_out);
  assign controlled_buffer_3_out = control_unit_1_mdrout_ib_eb ? MDR_q : 8'bz;  // Controlled_Buffer controlled_buffer_4
  assign controlled_buffer_3_out = control_unit_1_accout ? ACC_q : 8'bz;  // Controlled_Buffer controlled_buffer_5
  Register ACC (.D(multiplexer_3_out), .en(control_unit_1_accin), .Q(ACC_q), .clk(CLK));  // open: clr
  and JNE (JNE_out, control_unit_1_jne, zero_flag_qn);
  and JEQ (JEQ_out, control_unit_1_jeq, zero_flag_q);
  and JGT (JGT_out, control_unit_1_jgt, zero_flag_qn, Negative_Flag_qn);
  and JLT (JLT_out, control_unit_1_jlt, Negative_Flag_q);
  Hex_Digit_Display hex_digit_display_1 (.value(OUT_q_2));  // open: dp
  Hex_Digit_Display hex_digit_display_2 (.value(OUT_q));  // open: dp
  Register OUT (.D(controlled_buffer_3_out), .en(control_unit_1_outin), .Q({OUT_q_2, OUT_q}), .clk(CLK));  // open: clr
  Multiplexer #(.width(8), .enable("false")) multiplexer_3 (
    .in0(controlled_buffer_3_out), .in1(alu_1_p6), .out(multiplexer_3_out), .sel(control_unit_1_aluout));
  // ALU alu_1: pin names not known; wires that end beside it: controlled_buffer_3_out, ACC_q, control_unit_1_sub, control_unit_1_ash, control_unit_1_aluop, alu_1_p6
  D_Flip_Flop Negative_Flag (
    .clk(CLK), .D(alu_1_p6[7]), .Q(Negative_Flag_q), .Qn(Negative_Flag_qn), .en(control_unit_1_flagin));  // open: preset, reset
  nor nor_2 (nor_2_out, alu_1_p6[7], alu_1_p6[6], alu_1_p6[5], alu_1_p6[4], alu_1_p6[3], alu_1_p6[2], alu_1_p6[1], alu_1_p6[0]);
  D_Flip_Flop zero_flag (
    .clk(CLK), .D(nor_2_out), .Q(zero_flag_q), .Qn(zero_flag_qn), .en(control_unit_1_flagin));  // open: preset, reset
endmodule

module Control_Unit (
  input  [7:0] IR,
  input  in_2,
  output [2:0] ALUop,
  output MARin,
  output MDRout_IB_EB,
  output MDRin_IB_EB,
  output MDRin,
  output PCin,
  output PCout,
  output ACCin,
  output ACCout,
  output MemRead,
  output ash,
  output ALUout,
  output JEQ,
  output JNE,
  output JMP,
  output JGT,
  output JLT,
  output OUTin,
  output Flagin,
  output IRin,
  output HLT,
  output sub
);

  wire _1byte_alu_out, _2byte_out, and_1_out, and_2_out, and_3_out, and_4_out, and_5_out, and_6_out,
       and_8_out, and_9_out, and_10_out, and_11_out, and_12_out, and_13_out, and_14_out, and_15_out,
       and_16_out, and_17_out, and_19_out, and_20_out, and_27_out, and_28_out, decoder_1_out0,
       decoder_1_out1, decoder_1_out3, decoder_1_out4, decoder_1_out5, decoder_1_out6, decoder_1_out7,
       decoder_2_out0, decoder_2_out1, decoder_2_out2, decoder_2_out3, decoder_2_out4, decoder_2_out5,
       decoder_2_out6, decoder_2_out7, decoder_2_out8, decoder_2_out9, decoder_2_out10, decoder_2_out11,
       decoder_2_out12, decoder_2_out13, decoder_2_out14, decoder_2_out15, decoder_2_out16, decoder_2_out17,
       decoder_2_out18, decoder_2_out19, decoder_2_out20, decoder_2_out21, decoder_2_out22, decoder_2_out23,
       decoder_2_out24, decoder_2_out25, Fops_out, Fops_star_out, Iops_out, Jump_out, nor_1_out, not_1_out,
       not_2_out, or_1_out, or_2_out, or_3_out, or_5_out, or_6_out;
  wire [2:0] counter_1_out_3;

  Counter counter_1 (.out_3(counter_1_out_3), .in_2(or_1_out), .in_1(in_2));
  or or_1 (or_1_out, and_1_out, and_2_out);
  and and_1 (and_1_out, or_2_out, decoder_1_out6);
  and and_2 (and_2_out, decoder_1_out4, or_3_out);
  Decoder #(.select(3), .enable("false")) decoder_1 (
    .out0(decoder_1_out0), .out1(decoder_1_out1), .out2(IRin), .out3(decoder_1_out3), .out4(decoder_1_out4),
    .out5(decoder_1_out5), .out6(decoder_1_out6), .out7(decoder_1_out7), .sel(counter_1_out_3));
  or or_2 (or_2_out, decoder_2_out11, decoder_2_out12, decoder_2_out13, decoder_2_out14, decoder_2_out17, decoder_2_out19, decoder_2_out20, decoder_2_out21, decoder_2_out22, decoder_2_out23, decoder_2_out24);
  or or_3 (or_3_out, decoder_2_out6, decoder_2_out7, decoder_2_out8, decoder_2_out9, decoder_2_out10, decoder_2_out25, HLT);
  Decoder #(.select(5), .enable("false")) decoder_2 (
    .out0(decoder_2_out0), .out1(decoder_2_out1), .out2(decoder_2_out2), .out3(decoder_2_out3),
    .out4(decoder_2_out4), .out5(decoder_2_out5), .out6(decoder_2_out6), .out7(decoder_2_out7),
    .out8(decoder_2_out8), .out9(decoder_2_out9), .out10(decoder_2_out10), .out11(decoder_2_out11),
    .out12(decoder_2_out12), .out13(decoder_2_out13), .out14(decoder_2_out14), .out15(decoder_2_out15),
    .out16(decoder_2_out16), .out17(decoder_2_out17), .out18(decoder_2_out18), .out19(decoder_2_out19),
    .out20(decoder_2_out20), .out21(decoder_2_out21), .out22(decoder_2_out22), .out23(decoder_2_out23),
    .out24(decoder_2_out24), .out25(decoder_2_out25), .out26(HLT), .sel(IR[4:0]));  // open: out27, out28, out29, out30, out31
  or or_4 (sub, decoder_2_out1, decoder_2_out18, decoder_2_out19);
  or Fops (Fops_out, decoder_2_out0, decoder_2_out1, decoder_2_out2, decoder_2_out3, decoder_2_out4, decoder_2_out5, decoder_2_out15, decoder_2_out16, decoder_2_out18);
  or _2byte (_2byte_out, decoder_2_out24, decoder_2_out0, decoder_2_out1, decoder_2_out2, decoder_2_out3, decoder_2_out4, decoder_2_out5, decoder_2_out11, decoder_2_out12, decoder_2_out13, decoder_2_out14, decoder_2_out15, decoder_2_out16, decoder_2_out17, decoder_2_out18, decoder_2_out19, decoder_2_out20, decoder_2_out21, decoder_2_out22, decoder_2_out23);
  or Iops (Iops_out, decoder_2_out11, decoder_2_out12, decoder_2_out13, decoder_2_out14, decoder_2_out17, decoder_2_out19, decoder_2_out20, decoder_2_out21, decoder_2_out22, decoder_2_out23, decoder_2_out24);
  not not_1 (not_1_out, decoder_2_out16);
  or Jump (Jump_out, decoder_2_out20, decoder_2_out21, decoder_2_out22, decoder_2_out23, decoder_2_out24);
  or or_5 (or_5_out, decoder_2_out6, decoder_2_out7, decoder_2_out8, decoder_2_out9);
  nor nor_1 (nor_1_out, decoder_2_out19, decoder_2_out20, decoder_2_out21, decoder_2_out22, decoder_2_out23, decoder_2_out24);
  or or_6 (or_6_out, decoder_2_out0, decoder_2_out1, decoder_2_out2, decoder_2_out3, decoder_2_out4, decoder_2_out5, decoder_2_out15);
  or _1byte_alu (_1byte_alu_out, decoder_2_out6, decoder_2_out7, decoder_2_out8, decoder_2_out9, decoder_2_out10);
  or or_7 (ash, decoder_2_out8, decoder_2_out9);
  not not_2 (not_2_out, decoder_2_out17);
  or Fops_star (Fops_star_out, decoder_2_out0, decoder_2_out1, decoder_2_out2, decoder_2_out3, decoder_2_out5, decoder_2_out4, decoder_2_out19);
  ALU_Operation_Decoder alu_operation_decoder_1 (.in_1(IR[4:0]), .out_2(ALUop));
  and and_3 (and_3_out, _2byte_out, decoder_1_out3);
  and and_4 (and_4_out, Fops_out, decoder_1_out5);
  and and_5 (and_5_out, Iops_out, decoder_1_out5);
  and and_6 (and_6_out, Fops_out, not_1_out, decoder_1_out7);
  and and_7 (MDRin_IB_EB, decoder_2_out16, decoder_1_out6);
  and and_8 (and_8_out, Fops_out, decoder_1_out6);
  and and_9 (and_9_out, _2byte_out, decoder_1_out4);
  and and_10 (and_10_out, Jump_out, decoder_1_out5);
  and and_11 (and_11_out, _2byte_out, decoder_1_out3);
  and and_12 (and_12_out, or_5_out, decoder_1_out3);
  and and_13 (and_13_out, nor_1_out, Iops_out, decoder_1_out5);
  and and_14 (and_14_out, or_6_out, decoder_1_out7);
  and and_15 (and_15_out, decoder_1_out3, _1byte_alu_out);
  and and_16 (and_16_out, decoder_2_out16, decoder_1_out6);
  and and_17 (and_17_out, decoder_2_out25, decoder_1_out3);
  and and_18 (MemRead, decoder_2_out16, decoder_1_out7);
  and and_19 (and_19_out, Iops_out, not_2_out, decoder_1_out5);
  and and_20 (and_20_out, decoder_1_out7, Fops_star_out);
  and and_21 (JEQ, decoder_1_out5, decoder_2_out20);
  and and_22 (JNE, decoder_1_out5, decoder_2_out21);
  and and_23 (JMP, decoder_1_out5, decoder_2_out22);
  and and_24 (JGT, decoder_1_out5, decoder_2_out23);
  and and_25 (JLT, decoder_1_out5, decoder_2_out24);
  and and_26 (OUTin, decoder_1_out3, decoder_2_out25);
  and and_27 (and_27_out, decoder_2_out19, decoder_1_out5);
  and and_28 (and_28_out, decoder_2_out18, decoder_1_out7);
  or or_8 (ACCin, and_12_out, and_13_out, and_14_out, and_15_out);
  or or_9 (ACCout, and_16_out, and_17_out);
  or or_10 (ALUout, and_15_out, and_19_out, and_20_out);
  or or_11 (Flagin, and_27_out, and_28_out);
  or or_12 (MARin, decoder_1_out0, and_3_out, and_4_out);
  or or_13 (MDRout_IB_EB, and_4_out, and_5_out, IRin, and_6_out);
  or or_14 (MDRin, and_8_out, and_9_out, decoder_1_out1);
  or or_15 (PCin, and_10_out, decoder_1_out0, and_11_out);
  or or_16 (PCout, and_11_out, decoder_1_out0);
endmodule

module Counter (
  input  in_1,
  input  in_2,
  output [2:0] out_3
);

  wire and_1_out;

  and and_1 (and_1_out, out_3[0], out_3[1]);
  J_K_Flip_Flop j_k_ff_1 (
    .J(and_1_out), .clk(in_1), .K(and_1_out), .Q(out_3[2]), .reset(in_2));  // open: Qn, preset, en
  J_K_Flip_Flop j_k_ff_2 (.J(out_3[0]), .clk(in_1), .K(out_3[0]), .Q(out_3[1]), .reset(in_2));  // open: Qn, preset, en
  J_K_Flip_Flop j_k_ff_3 (.J(1'b1), .clk(in_1), .K(1'b1), .Q(out_3[0]), .reset(in_2));  // open: Qn, preset, en
endmodule

module ALU_Operation_Decoder (
  input  [4:0] in_1,
  output [2:0] out_2
);

  wire and_1_out, and_2_out, and_3_out, and_4_out, and_5_out, and_6_out, and_7_out, and_8_out, and_9_out,
       and_10_out, and_11_out, and_12_out, and_13_out, not_1_out, not_2_out, not_3_out, not_4_out, not_5_out,
       not_6_out, not_7_out, not_8_out, not_9_out, not_10_out, not_11_out, not_12_out, not_13_out,
       not_14_out, not_15_out, not_16_out, not_17_out, not_18_out, not_19_out, not_20_out, not_21_out;

  not not_1 (not_1_out, in_1[3]);
  not not_2 (not_2_out, in_1[0]);
  not not_3 (not_3_out, in_1[2]);
  not not_4 (not_4_out, in_1[1]);
  not not_5 (not_5_out, in_1[2]);
  not not_6 (not_6_out, in_1[0]);
  not not_7 (not_7_out, in_1[4]);
  not not_8 (not_8_out, in_1[3]);
  not not_9 (not_9_out, in_1[2]);
  not not_10 (not_10_out, in_1[2]);
  not not_11 (not_11_out, in_1[0]);
  not not_12 (not_12_out, in_1[1]);
  not not_13 (not_13_out, in_1[4]);
  not not_14 (not_14_out, in_1[3]);
  not not_15 (not_15_out, in_1[2]);
  not not_16 (not_16_out, in_1[1]);
  not not_17 (not_17_out, in_1[3]);
  not not_18 (not_18_out, in_1[0]);
  not not_19 (not_19_out, in_1[1]);
  not not_20 (not_20_out, in_1[2]);
  not not_21 (not_21_out, in_1[0]);
  and and_1 (and_1_out, not_1_out, in_1[2], not_2_out);
  and and_2 (and_2_out, in_1[2], in_1[1]);
  and and_3 (and_3_out, in_1[3], not_3_out, not_4_out);
  and and_4 (and_4_out, in_1[3], not_5_out, not_6_out);
  and and_5 (and_5_out, not_7_out, not_8_out, not_9_out, in_1[1]);
  and and_6 (and_6_out, in_1[2], in_1[1], in_1[0]);
  and and_7 (and_7_out, in_1[3], not_10_out, not_11_out);
  and and_8 (and_8_out, in_1[3], in_1[2], not_12_out);
  and and_9 (and_9_out, not_13_out, not_14_out, not_15_out, in_1[1], in_1[0]);
  and and_10 (and_10_out, in_1[2], not_16_out, in_1[0]);
  and and_11 (and_11_out, not_17_out, in_1[2], in_1[1], not_18_out);
  and and_12 (and_12_out, in_1[3], not_19_out, in_1[0]);
  and and_13 (and_13_out, in_1[3], not_20_out, in_1[1], not_21_out);
  or or_1 (out_2[2], and_1_out, and_2_out, and_3_out, and_4_out);
  or or_2 (out_2[1], and_5_out, and_6_out, and_7_out, and_8_out);
  or or_3 (out_2[0], and_9_out, and_10_out, and_11_out, and_12_out, and_13_out);
endmodule
